# Fritzing sketch SensorPesoHX711 (saved by Fritzing 0.9.3b)

parts:
  Load_Cell1 = Load Cell - Red/white/black/green
  Part1 = HX711 Weighing Sensor Module
  M5Stack_Core_(Back)1 = M5Stack Core (Back)

nets:
  N1: Load_Cell1.wire1, Part1.E+
  N2: Load_Cell1.wire2, Part1.A+
  N3: Load_Cell1.wire3, Part1.E-
  N4: Load_Cell1.wire4, Part1.A-
  VCC: Part1.VCC, M5Stack_Core_(Back)1.5V
  GND: Part1.GND, M5Stack_Core_(Back)1.Gnd
  N5: Part1.DO/RX, M5Stack_Core_(Back)1.5
  N6: Part1.CK/TX, M5Stack_Core_(Back)1.G2

custom parts:
  Load Cell - Red/white/black/green: A rectangle load cell/weighting pressure Sensor with four wires - Red, white, black, green. Normally corresponding with E+, E-, A+, A- respectively.
  HX711 Weighing Sensor Module: HX711 is a precision 24-bit analog-to-digital converter (ADC) designed for weigh scales and industrial control applications to interface directly with a bridge sensor.
  M5Stack Core (Back): M5Stack ESP32 development kit
