# Fritzing sketch RFID (saved by Fritzing 0.9.3b)

parts:
  Part2 = RFID-RC522 [part_number=101218]
  M5Stack_Core_(Back)2 = M5Stack Core (Back)

nets:
  N1: Part2.SDA, M5Stack_Core_(Back)2.DA
  N2: Part2.SCK, M5Stack_Core_(Back)2.SCK
  N3: Part2.MOSI, M5Stack_Core_(Back)2.MO
  N4: Part2.MISO, M5Stack_Core_(Back)2.19
  GND: Part2.GND, M5Stack_Core_(Back)2.Gnd
  3.3V: Part2.3.3V, M5Stack_Core_(Back)2.3V3

custom parts:
  M5Stack Core (Back): M5Stack ESP32 development kit
