# Fritzing sketch SensorHumedadTemperatura (saved by Fritzing 0.9.3b)

parts:
  DHT2 = DHT11 Humitidy and Temperature Sensor  # not connected
  J1 = Dagu DGServo 9g header (male) [package=THT]
  Componente3 = YC164 [package=YC164]
  Componente4 = YC164 [package=YC164]
  Componente5 = YC164 [package=YC164]  # not connected
  Componente6 = YC164 [part_number="S + -" package=YC164]  # not connected
  Componente7 = YC164 [package=YC164]  # not connected
  M5Stack_Core_(Back)1 = M5Stack Core (Back)

nets:
  N1: J1.gnd, Componente3.3, Componente4.1, M5Stack_Core_(Back)1.26
  VCC: J1.Vcc, Componente3.4, Componente4.2, M5Stack_Core_(Back)1.5V
  N2: J1.Señal, Componente4.3, M5Stack_Core_(Back)1.Gnd

custom parts:
  DHT11 Humitidy and Temperature Sensor: DHT11 Humidity and Temperature Sensor
  Dagu DGServo 9g header (male): Dagu DGServo 9g header (male) This part is a minor variation of the standard three pin header; in schematic view the pins have been labelled to show clearly pulse, Vcc and ground. Plug this header into a breadboard, stripboard or PCB to allow a servo header female connector plug (e.g. on the Dagu DGServo 9g) to be connected to the board.
  M5Stack Core (Back): M5Stack ESP32 development kit
